# Fritzing sketch DHT_Scheme (saved by Fritzing 0.9.3b)

parts:
  U1 = ESP8266 WiFi Module [part_number=ESP8266]
  DHT1 = DHT22 Humidity and Temperature Sensor

nets:
  VCC: U1.VCC, DHT1.VDD
  N1: U1.GPIO_0, DHT1.DATA
  GND: U1.GND, DHT1.GND

custom parts:
  ESP8266 WiFi Module: Generic WiFi Module based on the ESP8266 with onboard PCB antenna and UART communications
